# Fritzing sketch Diagram (saved by Fritzing 0.9.4)
breadboards: 1

parts:
  Part1 = Arduino Uno (Rev3)
  Part2 = RFID-RC522-v3
  U1 = NodeMCU V1.0
  S1 = Pushbutton [package="[THT]"]
  LED1 = smd LED [color="Red (633nm)" package="0603 [SMD]"]
  R1 = Resistor [tolerance=±5% resistance=1k package=THT]
  R2 = Resistor [tolerance=±5% resistance=1k package=THT]

nets:
  N1: Part1.D9_PWM, Part2.RST
  N2: Part1.D10_PWM/SS, Part2.SDA
  N3: Part1.D11_PWM/MOSI, Part2.MOSI
  N4: Part1.D12/MISO, Part2.MISO
  N5: Part1.D13/SCK, Part2.SCK
  N6: Part1.D2, U1.D2
  N7: Part1.D3_PWM, U1.D3
  N8: Part1.D4, R1.Pin_0
  3V3: Part1.3V3, Part2.3.3V
  N9: Part1.5V, S1.Pin_1, S1.Pin_2
  GND: Part1.GND, Part2.GND, U1.GND, LED1.cathode, R2.Pin_0
  VIN: Part1.VIN, U1.Vin
  N10: U1.D5, S1.Pin_3, S1.Pin_4, R2.Pin_1
  N11: LED1.anode, R1.Pin_1

custom parts:
  RFID-RC522-v3: A simple China made RFID-RC522 Reader (6x4 cm); do check the pin labels, as this is a MFRC522 based clone.
  NodeMCU V1.0: ESP8266 based NodeMCU
